// Logisim project 8255.circ as structural Verilog: 5 circuits, main circuit full
// PA
module port_A (
  input  [7:0] D,
  input  [7:0] InPort,
  input  Clc,
  input  Enable,
  input  [7:0] InBus,
  output [7:0] OutBus,
  output [7:0] OutPort
);

  wire and_1_out, and_2_out, and_3_out, and_4_out, and_5_out, not_1_out, not_2_out, not_3_out, not_4_out,
       or_1_out;
  wire [7:0] register_1_q;

  or or_1 (or_1_out, D[6], D[5]);
  not not_1 (not_1_out, D[5]);
  and and_1 (and_1_out, not_1_out, not_2_out);
  not not_2 (not_2_out, D[6]);
  and and_2 (and_2_out, D[4], or_1_out);
  not not_3 (not_3_out, and_5_out);
  assign OutBus = not_3_out ? register_1_q : 8'bz;  // Controlled_Buffer controlled_buffer_1
  and and_3 (and_3_out, and_2_out, Enable);
  and and_4 (and_4_out, Enable, not_4_out);
  not not_4 (not_4_out, D[4]);
  and and_5 (and_5_out, D[4], Enable, and_1_out);
  assign OutBus = and_5_out ? InPort : 8'bz;  // Controlled_Buffer controlled_buffer_2
  Register register_1 (.D(InPort), .en(and_3_out), .Q(register_1_q), .clk(Clc));  // open: clr
  Register register_2 (.D(InBus), .en(and_4_out), .Q(OutPort), .clk(Clc));  // open: clr
endmodule

// PB
module port_B (
  input  [7:0] D,
  input  [7:0] InPort,
  input  Clc,
  input  Enable,
  input  [7:0] InBus,
  output [7:0] OutBus,
  output [7:0] OutPort
);

  wire and_1_out, and_2_out, and_3_out, and_4_out, not_1_out, not_2_out, not_3_out;
  wire [7:0] register_1_q;

  and and_1 (and_1_out, D[1], D[2]);
  not not_1 (not_1_out, and_4_out);
  assign OutBus = not_1_out ? register_1_q : 8'bz;  // Controlled_Buffer controlled_buffer_1
  and and_2 (and_2_out, and_1_out, Enable);
  and and_3 (and_3_out, Enable, not_2_out);
  not not_2 (not_2_out, D[1]);
  not not_3 (not_3_out, D[2]);
  and and_4 (and_4_out, D[1], Enable, not_3_out);
  assign OutBus = and_4_out ? InPort : 8'bz;  // Controlled_Buffer controlled_buffer_2
  Register register_1 (.D(InPort), .en(and_2_out), .Q(register_1_q), .clk(Clc));  // open: clr
  Register register_2 (.D(InBus), .en(and_3_out), .Q(OutPort), .clk(Clc));  // open: clr
endmodule

module full (
  input  [7:0] in_1,
  input  [7:0] in_2,
  input  [7:0] in_3,
  input  RD,
  input  [3:0] in_5,
  input  WR,
  input  [3:0] in_7,
  input  CS,
  input  A0,
  input  A1,
  output [7:0] out_11,
  output [7:0] out_12,
  output [7:0] out_13,
  output [3:0] out_14,
  output [3:0] out_15
);

  wire clock_1_out, decoder_1_out0, decoder_1_out1, decoder_1_out2, decoder_1_out3, not_1_out, not_2_out,
       not_3_out;
  wire [7:0] controlled_buffer_2_out, controlled_buffer_3_out, ControlReg_q, port_a_1_outbus,
       port_b_1_outbus, portc_low_1_outbus, undriven;

  not not_1 (not_1_out, RD);
  not not_2 (not_2_out, WR);
  assign out_11 = not_2_out ? controlled_buffer_3_out : 8'bz;  // Controlled_Buffer controlled_buffer_1
  assign controlled_buffer_2_out = not_1_out ? in_2 : 8'bz;  // Controlled_Buffer controlled_buffer_2
  not not_3 (not_3_out, CS);
  Decoder #(.select(2)) decoder_1 (
    .out0(decoder_1_out0), .out1(decoder_1_out1), .out2(decoder_1_out2), .out3(decoder_1_out3),
    .sel({A1, A0}), .en(not_3_out));
  assign controlled_buffer_3_out = decoder_1_out2 ? portc_low_1_outbus : 8'bz;  // Controlled_Buffer controlled_buffer_3
  assign controlled_buffer_3_out = decoder_1_out2 ? undriven : 8'bz;  // Controlled_Buffer controlled_buffer_4
  assign controlled_buffer_3_out = decoder_1_out0 ? port_a_1_outbus : 8'bz;  // Controlled_Buffer controlled_buffer_5
  assign controlled_buffer_3_out = decoder_1_out1 ? port_b_1_outbus : 8'bz;  // Controlled_Buffer controlled_buffer_6
  Register ControlReg (
    .D(controlled_buffer_2_out), .en(decoder_1_out3), .Q(ControlReg_q), .clk(clock_1_out));  // open: clr
  Clock clock_1 (.out(clock_1_out));
  port_A port_a_1 (
    .D(ControlReg_q), .OutBus(port_a_1_outbus), .Enable(decoder_1_out0), .InBus(controlled_buffer_2_out),
    .InPort(in_1), .Clc(clock_1_out), .OutPort(out_12));
  port_B port_b_1 (
    .D(ControlReg_q), .OutBus(port_b_1_outbus), .Enable(decoder_1_out1), .InBus(controlled_buffer_2_out),
    .InPort(in_3), .Clc(clock_1_out), .OutPort(out_13));
  portC_low portc_low_1 (
    .D(ControlReg_q), .OutBus(portc_low_1_outbus[3:0]), .Enable(decoder_1_out2), .InBus(undriven[3:0]),
    .InPort(in_5), .Clc(clock_1_out), .OutPort(out_14));
  portC_high portc_high_1 (
    .D(ControlReg_q), .OutBus(portc_low_1_outbus[7:4]), .Enable(decoder_1_out2), .InBus(undriven[7:4]),
    .InPort(in_7), .Clc(clock_1_out), .OutPort(out_15));
endmodule

// PCl
module portC_low (
  input  [7:0] D,
  input  [3:0] InPort,
  input  Clc,
  input  Enable,
  input  [3:0] InBus,
  output [3:0] OutBus,
  output [3:0] OutPort
);

  wire and_1_out, and_2_out, and_3_out, and_4_out, not_1_out, not_2_out, not_3_out;
  wire [3:0] register_1_q;

  D_Flip_Flop d_ff_1 ();  // open: clk, D, Q, Qn, preset, en, reset
  D_Flip_Flop d_ff_2 ();  // open: clk, D, Q, Qn, preset, en, reset
  and and_1 (and_1_out, D[0], D[2]);
  not not_1 (not_1_out, and_4_out);
  assign OutBus = not_1_out ? register_1_q : 4'bz;  // Controlled_Buffer controlled_buffer_1
  and and_2 (and_2_out, and_1_out, Enable);
  and and_3 (and_3_out, Enable, not_2_out);
  not not_2 (not_2_out, D[0]);
  not not_3 (not_3_out, D[2]);
  and and_4 (and_4_out, D[0], Enable, not_3_out);
  assign OutBus = and_4_out ? InPort : 4'bz;  // Controlled_Buffer controlled_buffer_2
  Register #(.width(4)) register_1 (.D(InPort), .en(and_2_out), .Q(register_1_q), .clk(Clc));  // open: clr
  Register #(.width(4)) register_2 (.D(InBus), .en(and_3_out), .Q(OutPort), .clk(Clc));  // open: clr
endmodule

// PCh
module portC_high (
  input  [7:0] D,
  input  [3:0] InPort,
  input  Clc,
  input  Enable,
  input  [3:0] InBus,
  output [3:0] OutBus,
  output [3:0] OutPort
);

  wire and_1_out, and_2_out, and_3_out, and_4_out, and_5_out, not_1_out, not_2_out, not_3_out, not_4_out,
       or_1_out;
  wire [3:0] register_1_q;

  or or_1 (or_1_out, D[6], D[5]);
  not not_1 (not_1_out, D[5]);
  and and_1 (and_1_out, not_1_out, not_2_out);
  not not_2 (not_2_out, D[6]);
  and and_2 (and_2_out, D[3], or_1_out);
  not not_3 (not_3_out, and_5_out);
  assign OutBus = not_3_out ? register_1_q : 4'bz;  // Controlled_Buffer controlled_buffer_1
  and and_3 (and_3_out, and_2_out, Enable);
  and and_4 (and_4_out, Enable, not_4_out);
  not not_4 (not_4_out, D[3]);
  and and_5 (and_5_out, D[3], Enable, and_1_out);
  assign OutBus = and_5_out ? InPort : 4'bz;  // Controlled_Buffer controlled_buffer_2
  Register #(.width(4)) register_1 (.D(InPort), .en(and_3_out), .Q(register_1_q), .clk(Clc));  // open: clr
  Register #(.width(4)) register_2 (.D(InBus), .en(and_4_out), .Q(OutPort), .clk(Clc));  // open: clr
endmodule
